# Fritzing sketch SN74HC595 drives 4-digit digital tube (saved by Fritzing 0.9.3b)
breadboards: 1

parts:
  D1 = Rectifier Diode [part_number=1N4001 package="300 mil [THT]"]  # not connected
  C1 = Electrolytic Capacitor [package="100 mil [THT, electrolytic]"]  # not connected
  L1 = Inductor [package="400 mil [THT]"]  # not connected
  RHT1 = Humidity and Temperature Sensor RHT03
  U1 = SN74LS21N [package="DIP14 [THT]"]

nets:
  N1: RHT1.Data-signal, U1.2C
  N2: RHT1.GND_1, U1.1D
  N3: RHT1.pin_13, U1.1A
  N4: RHT1.pin_14, U1.1C
  N5: RHT1.pin_15, U1.NC#2
  N6: RHT1.pin_16, U1.GND
  N7: RHT1.pin_17, U1.1B
  N8: RHT1.pin_18, U1.1Y
  N9: U1.VCC, U1.pin_15

custom parts:
  Rectifier Diode: A standard rectifier diode
  Electrolytic Capacitor: A small electrolytic capacitor
  Humidity and Temperature Sensor RHT03: Digital relative humidity & temperature sensor RHT03
  SN74LS21N: Dual 4-input positive-AND gates
