# Fritzing sketch Serial LCD1602 dynamic display experiment (saved by Fritzing 0.9.3b)

parts:
  D1 = Rectifier Diode [part_number=1N4001 package="300 mil [THT]"]  # not connected
  S1 = Tilt Switch [package=THT]
  U1 = Mystery Part - 3 pins [chip_label=? package=THT]
  S2 = Tilt Switch [package=THT]

nets:
  N1: S1.pin_106, U1.pin2, S2.pin_66, S2.pin_106
  N2: S1.pin_107, U1.pin1, S2.pin_107
  N3: S1.pin_108, U1.pin3, S2.pin_108
  N4: S1.pin_109, U1.pin_4, S2.pin_109

custom parts:
  Rectifier Diode: A standard rectifier diode
  Mystery Part - 3 pins: A dummy, proxy, ersatz, stand-in part for whatever you want. With 3 pins on a 100 mil inline pin header footprint.
