# Fritzing sketch Photosensitive resistance component experiment (saved by Fritzing 0.9.3b)
breadboards: 1

parts:
  D1 = Rectifier Diode [part_number=1N4001 package="300 mil [THT]"]  # not connected
  S1 = Tilt Switch [package=THT]
  LED1 = LED - 5mm [color="Red (633nm)" package="5 mm [THT]"]
  R1 = Resistor [tolerance=±5% resistance=220 package=THT]
  R2 = Photocell (LDR) [package=THT]
  R3 = Resistor [tolerance=±5% resistance=220 package=THT]

nets:
  N1: S1.pin_64, R3.Pin_1
  N2: S1.pin_66, R2.pin_0
  N3: S1.pin_103, LED1.cathode
  N4: S1.pin_105, R1.Pin_1
  N5: LED1.anode, R1.Pin_0
  N6: R2.pin_1, R3.Pin_0

custom parts:
  Rectifier Diode: A standard rectifier diode
