# Fritzing sketch Infrared transmission experiment (saved by Fritzing 0.9.3b)

parts:
  D1 = Rectifier Diode [part_number=1N4001 package="300 mil [THT]"]  # not connected
  S1 = Tilt Switch [package=THT]
  R1 = 220 Ω Resistor [package=THT]
  R2 = 220 Ω Resistor [package=THT]

nets:
  N1: S1.pin_49, R2.pin_2
  N2: S1.pin_51, R2.pin_3
  N3: S1.pin_52, R1.pin_3
  N4: S1.pin_53, R1.pin_4
  N5: S1.pin_54, R1.pin_2

custom parts:
  Rectifier Diode: A standard rectifier diode
  220 Ω Resistor: A generic resistor (0.25W)
  220 Ω Resistor: A generic resistor (0.25W)
