# Fritzing sketch Infrared remote control module experiment (saved by Fritzing 0.9.3b)

parts:
  D1 = Rectifier Diode [part_number=1N4001 package="300 mil [THT]"]  # not connected
  S1 = Tilt Switch [package=THT]
  R2 = 220 Ω Resistor [package=THT]  # not connected
  R3 = 220 Ω Resistor [package=THT]

nets:
  N1: S1.pin_52, R3.pin_7
  N2: S1.pin_53, R3.pin_6
  N3: S1.pin_54, R3.pin_5

custom parts:
  Rectifier Diode: A standard rectifier diode
  220 Ω Resistor: A generic resistor (0.25W)
  220 Ω Resistor: A generic resistor (0.25W)
