# Fritzing sketch Potentiometer adjustment steering gear experiment (saved by Fritzing 0.9.3b)

parts:
  D1 = Rectifier Diode [part_number=1N4001 package="300 mil [THT]"]  # not connected
  S1 = Tilt Switch [package=THT]
  R1 = Rotary Potentiometer (Small) [maximum_resistance=100kΩ package=THT]
  J1 = Basic Servo

nets:
  N1: S1.pin_55, J1.gnd
  N2: S1.pin_56, J1.vcc
  N3: S1.pin_57, J1.pulse
  N4: S1.pin_64, R1.leg2
  N5: S1.pin_65, R1.leg1
  N6: S1.pin_66, R1.wiper

custom parts:
  Rectifier Diode: A standard rectifier diode
