# Fritzing sketch LED water lamp experiment (saved by Fritzing 0.9.3b)
breadboards: 1

parts:
  D1 = Rectifier Diode [part_number=1N4001 package="300 mil [THT]"]  # not connected
  LED1 = LED - 5mm [color="Red (633nm)" package="5 mm [THT]"]
  LED2 = LED - 5mm [color="Red (633nm)" package="5 mm [THT]"]
  LED3 = LED - 5mm [color="Red (633nm)" package="5 mm [THT]"]
  LED4 = LED - 5mm [color="Red (633nm)" package="5 mm [THT]"]
  LED5 = LED - 5mm [color="Red (633nm)" package="5 mm [THT]"]
  LED6 = LED - 5mm [color="Red (633nm)" package="5 mm [THT]"]
  R1 = Resistor [tolerance=±5% resistance=220 package=THT]
  R2 = Resistor [tolerance=±5% resistance=220 package=THT]
  R3 = Resistor [tolerance=±5% resistance=220 package=THT]
  R4 = Resistor [tolerance=±5% resistance=220 package=THT]
  R5 = Resistor [tolerance=±5% resistance=220 package=THT]
  R6 = Resistor [tolerance=±5% resistance=220 package=THT]
  C1 = Electrolytic Capacitor [package="100 mil [THT, electrolytic]"]  # not connected
  L1 = Inductor [package="400 mil [THT]"]  # not connected

nets:
  N1: LED1.cathode, LED2.cathode, LED3.cathode, LED4.cathode, LED5.cathode, LED6.cathode
  N2: LED1.anode, R2.Pin_1
  N3: LED2.anode, R3.Pin_1
  N4: LED3.anode, R4.Pin_1
  N5: LED4.anode, R5.Pin_1
  N6: LED5.anode, R6.Pin_1
  N7: LED6.anode, R1.Pin_1

custom parts:
  Rectifier Diode: A standard rectifier diode
  Electrolytic Capacitor: A small electrolytic capacitor
