# Fritzing sketch DS1302 electronic clock module experiment (saved by Fritzing 0.9.3b)

parts:
  D1 = Rectifier Diode [part_number=1N4001 package="300 mil [THT]"]  # not connected
  S1 = Tilt Switch [package=THT]
  U1 = Mystery Part - 3 pins [chip_label=? package=THT]
  R1 = 220 Ω Resistor [package=THT]

nets:
  N1: S1.pin_51, R1.pin_4
  N2: S1.pin_52, R1.pin_2
  N3: S1.pin_54, R1.pin_5
  N4: S1.pin_57, R1.pin_3
  N5: S1.pin_106, U1.pin2
  N6: S1.pin_107, U1.pin1
  N7: S1.pin_108, U1.pin3
  N8: S1.pin_109, U1.pin_4

custom parts:
  Rectifier Diode: A standard rectifier diode
  Mystery Part - 3 pins: A dummy, proxy, ersatz, stand-in part for whatever you want. With 3 pins on a 100 mil inline pin header footprint.
  220 Ω Resistor: A generic resistor (0.25W)
