# Fritzing sketch Game control five-way button module experiment (saved by Fritzing 0.9.3b)
breadboards: 1

parts:
  LED1 = LED - 5mm [color="Red (633nm)" package="5 mm [THT]"]
  LED2 = LED - 5mm [color="Red (633nm)" package="5 mm [THT]"]
  LED3 = LED - 5mm [color="Red (633nm)" package="5 mm [THT]"]
  LED4 = LED - 5mm [color="Red (633nm)" package="5 mm [THT]"]
  R2 = Resistor [tolerance=±5% resistance=220 package=THT]
  R3 = Resistor [tolerance=±5% resistance=220 package=THT]
  R4 = Resistor [tolerance=±5% resistance=220 package=THT]
  R5 = Resistor [tolerance=±5% resistance=220 package=THT]
  D1 = Rectifier Diode [part_number=1N4001 package="300 mil [THT]"]  # not connected
  S1 = Tilt Switch [package=THT]
  R6 = Resistor [tolerance=±5% resistance=220 package=THT]
  LED5 = LED - 5mm [color="Red (633nm)" package="5 mm [THT]"]
  MIC1 = Microphone

nets:
  N1: LED1.cathode, LED2.cathode, LED3.cathode, LED4.cathode, S1.pin_88, LED5.cathode
  N2: LED1.anode, R2.Pin_1
  N3: LED2.anode, R3.Pin_1
  N4: LED3.anode, R4.Pin_1
  N5: LED4.anode, R5.Pin_1
  N6: R2.Pin_0, S1.pin_90
  N7: R3.Pin_0, S1.pin_93
  N8: R4.Pin_0, S1.pin_96
  N9: R5.Pin_0, S1.pin_99
  N10: S1.pin_51, MIC1.pin_5
  N11: S1.pin_66, MIC1.pin_3
  N12: S1.pin_68, MIC1.pin_7
  N13: S1.pin_69, MIC1.pin_4
  N14: S1.pin_102, R6.Pin_0
  N15: R6.Pin_1, LED5.anode

custom parts:
  Rectifier Diode: A standard rectifier diode
