# Fritzing sketch Hall switch experiment (saved by Fritzing 0.9.3b)
breadboards: 1

parts:
  D1 = Rectifier Diode [part_number=1N4001 package="300 mil [THT]"]  # not connected
  S1 = Tilt Switch [package=THT]
  Q1 = PNP-Transistor [package="TO92 [THT]"]
  LED1 = LED - 5mm [color="Red (633nm)" package="5 mm [THT]"]
  R1 = Resistor [tolerance=±5% resistance=220 package=THT]
  J1 = Piezo Speaker

nets:
  N1: S1.pin_88, Q1.B, J1.pin1
  N2: S1.pin_89, Q1.E
  N3: S1.pin_90, Q1.C
  N4: S1.pin_93, R1.Pin_1
  N5: S1.pin_96, J1.pin2
  N6: LED1.anode, R1.Pin_0

custom parts:
  Rectifier Diode: A standard rectifier diode
