# Fritzing sketch Tilt switch experiment (saved by Fritzing 0.9.3b)
breadboards: 1

parts:
  D1 = Rectifier Diode [part_number=1N4001 package="300 mil [THT]"]  # not connected
  C1 = Electrolytic Capacitor [package="100 mil [THT, electrolytic]"]  # not connected
  L1 = Inductor [package="400 mil [THT]"]
  C2 = Electrolytic Capacitor [capacitance=1µF package="100 mil [THT, electrolytic]"]
  R1 = Resistor [tolerance=±5% resistance=220 package=THT]
  J1 = Piezo Speaker
  LED1 = LED - 5mm [color="Red (633nm)" package="5 mm [THT]"]

nets:
  N1: L1.pin_0, L1.pin_1
  N2: C2.+, J1.pin1, LED1.cathode
  N3: R1.Pin_0, LED1.anode

custom parts:
  Rectifier Diode: A standard rectifier diode
  Electrolytic Capacitor: A small electrolytic capacitor
