# Fritzing sketch Four-way answerer experiment (saved by Fritzing 0.9.3b)
breadboards: 1

parts:
  D1 = Rectifier Diode [part_number=1N4001 package="300 mil [THT]"]  # not connected
  S1 = Tilt Switch [package=THT]
  LED1 = LED - 5mm [color="Red (633nm)" package="5 mm [THT]"]
  7_Segment1 = 7 Segment Display  # not connected
  LED2 = RGB LED (com. cathode, rgb) [package="5 mm [THT]"]
  LED3 = RGB LED (com. cathode, rgb) [package="5 mm [THT]"]
  R1 = Resistor [tolerance=±5% resistance=220 package=THT]  # not connected
  R2 = Resistor [tolerance=±5% resistance=220 package=THT]
  R3 = Resistor [tolerance=±5% resistance=220 package=THT]
  R4 = Resistor [tolerance=±5% resistance=220 package=THT]
  S2 = Pushbutton [package="[THT]"]
  S3 = Pushbutton [package="[THT]"]
  S4 = Pushbutton [package="[THT]"]
  S5 = Pushbutton [package="[THT]"]

nets:
  N1: S1.pin_49, LED1.cathode, LED2.red_anode, LED3.red_anode
  N2: S1.pin_54, R2.Pin_0
  N3: S1.pin_57, R3.Pin_0
  N4: S1.pin_60, R4.Pin_0
  N5: S1.pin_90, S2.Pin_1, S2.Pin_2
  N6: S1.pin_93, S3.Pin_1, S3.Pin_2
  N7: S1.pin_96, S4.Pin_1, S4.Pin_2
  N8: S1.pin_99, S5.Pin_1, S5.Pin_2
  N9: LED2.common_cathode, R3.Pin_1
  N10: LED3.common_cathode, R4.Pin_1
  N11: S2.Pin_3, S2.Pin_4, S3.Pin_3, S3.Pin_4, S4.Pin_3, S4.Pin_4, S5.Pin_3, S5.Pin_4

custom parts:
  Rectifier Diode: A standard rectifier diode
  7 Segment Display: 7 Segment Display with common anode.
  RGB LED (com. cathode, rgb): A 5mm tri-color LED with red, green and blue inside.
  RGB LED (com. cathode, rgb): A 5mm tri-color LED with red, green and blue inside.
