# Fritzing sketch Sound sensor module experiment (saved by Fritzing 0.9.3b)
breadboards: 1

parts:
  D1 = Rectifier Diode [part_number=1N4001 package="300 mil [THT]"]  # not connected
  S1 = Tilt Switch [package=THT]
  R3 = Basic Flex Resistor
  LED1 = LED - 5mm [color="Red (633nm)" package="5 mm [THT]"]
  R4 = Resistor [tolerance=±5% resistance=220 package=THT]

nets:
  N1: S1.pin_52, LED1.cathode
  N2: S1.pin_54, R4.Pin_1
  N3: S1.pin_64, S1.pin_65, S1.pin_66
  N4: R3.Pin_2, R3.pin_3, R3.pin_4, R3.pin_5
  N5: LED1.anode, R4.Pin_0

custom parts:
  Rectifier Diode: A standard rectifier diode
  Basic Flex Resistor: A generic Flex resistor
