# Fritzing sketch Water depth sensor module experiment (saved by Fritzing 0.9.3b)

parts:
  D1 = Rectifier Diode [part_number=1N4001 package="300 mil [THT]"]  # not connected
  S1 = Tilt Switch [package=THT]
  LED1 = Red LED - 5mm [package="5 mm [THT]"]

nets:
  N1: S1.pin_64, LED1.pin_2
  N2: S1.pin_65, LED1.pin_3
  N3: S1.pin_66, LED1.pin_4

custom parts:
  Rectifier Diode: A standard rectifier diode
  Red LED - 5mm: A generic red LED (~1.8V)
