# Fritzing sketch Remote control shaking head fan experiment (saved by Fritzing 0.9.3b)

parts:
  D1 = Rectifier Diode [part_number=1N4001 package="300 mil [THT]"]  # not connected
  S1 = Tilt Switch [package=THT]
  R2 = 220 Ω Resistor [package=THT]  # not connected
  R3 = 220 Ω Resistor [package=THT]
  J1 = Peltier Element
  J2 = Basic Servo
  M1 = DC Motor

nets:
  N1: S1.pin_13, J1.pin_13
  N2: S1.pin_14, J1.pin_14
  N3: S1.pin_15, J1.pin_4
  N4: S1.pin_52, R3.pin_7
  N5: S1.pin_53, R3.pin_6
  N6: S1.pin_54, R3.pin_5
  N7: S1.pin_55, J2.gnd
  N8: S1.pin_56, J2.vcc
  N9: S1.pin_57, J2.pulse
  N10: J1.pin_11, M1.pin_1
  N11: J1.pin_12, M1.pin_2

custom parts:
  Rectifier Diode: A standard rectifier diode
  220 Ω Resistor: A generic resistor (0.25W)
  220 Ω Resistor: A generic resistor (0.25W)
