# Fritzing sketch RGB lamp beads experiment (saved by Fritzing 0.9.3b)
breadboards: 1

parts:
  D1 = Rectifier Diode [part_number=1N4001 package="300 mil [THT]"]  # not connected
  R2 = Resistor [tolerance=±5% resistance=220 package=THT]
  R3 = Resistor [tolerance=±5% resistance=220 package=THT]
  R4 = Resistor [tolerance=±5% resistance=220 package=THT]
  LED1 = RGB LED (com. cathode, rgb) [package="5 mm [THT]"]
  C1 = Electrolytic Capacitor [package="100 mil [THT, electrolytic]"]  # not connected
  L1 = Inductor [package="400 mil [THT]"]

nets:
  N1: R2.Pin_1, LED1.red_anode
  N2: R3.Pin_1, LED1.green_anode
  N3: R4.Pin_1, LED1.blue_anode
  N4: L1.pin_0, L1.pin_1

custom parts:
  Rectifier Diode: A standard rectifier diode
  Electrolytic Capacitor: A small electrolytic capacitor
