# Fritzing sketch Key module experiment (saved by Fritzing 0.9.3b)
breadboards: 1

parts:
  D1 = Rectifier Diode [part_number=1N4001 package="300 mil [THT]"]
  R2 = Resistor [tolerance=±5% resistance=220 package=THT]
  R4 = Resistor [tolerance=±5% resistance=220 package=THT]
  LED1 = LED - 5mm [color="Red (633nm)" package="5 mm [THT]"]
  S1 = Pushbutton [package="[THT]"]
  S2 = Tilt Switch [package=THT]

nets:
  N1: D1.pin_2, D1.pin_3, D1.pin_4, D1.pin_5, D1.pin_7, D1.pin_8, D1.pin_9, D1.pin_10, D1.pin_11, D1.pin_13, D1.pin_14, D1.pin_15, D1.pin_16, D1.pin_17, D1.pin_19, R4.Pin_0, LED1.cathode, S2.pin_49
  N2: R2.Pin_1, LED1.anode
  N3: R4.Pin_1, S1.Pin_1, S1.Pin_2
  N4: S1.Pin_3, S1.Pin_4, S2.pin_50

custom parts:
  Rectifier Diode: A standard rectifier diode
