# Fritzing sketch Buzzer experiment (saved by Fritzing 0.9.3b)
breadboards: 1

parts:
  D1 = Rectifier Diode [part_number=1N4001 package="300 mil [THT]"]  # not connected
  C1 = Electrolytic Capacitor [package="100 mil [THT, electrolytic]"]  # not connected
  L1 = Inductor [package="400 mil [THT]"]
  J1 = Piezo Speaker  # not connected

nets:
  N1: L1.pin_0, L1.pin_1

custom parts:
  Rectifier Diode: A standard rectifier diode
  Electrolytic Capacitor: A small electrolytic capacitor
