# Fritzing sketch Thermistor experiment (saved by Fritzing 0.9.3b)
breadboards: 1

parts:
  D1 = Rectifier Diode [part_number=1N4001 package="300 mil [THT]"]  # not connected
  S1 = Tilt Switch [package=THT]
  R1 = Resistor [tolerance=±5% resistance=220 package=THT]
  LED1 = LED - 5mm [color="Red (633nm)" package="5 mm [THT]"]
  R2 = Resistor [tolerance=±5% resistance=220 package=THT]
  元件1 = LSM303C (6 DOF)  # not connected

nets:
  N1: S1.pin_64, R2.Pin_0
  N2: S1.pin_66, R2.Pin_1
  N3: S1.pin_94, LED1.cathode
  N4: S1.pin_96, R1.Pin_1
  N5: R1.Pin_0, LED1.anode

custom parts:
  Rectifier Diode: A standard rectifier diode
  LSM303C (6 DOF): SparkFun 6 Degrees of Freedom Breakout - LSM303C The LSM303C is a 6 Degrees of Freedom (6DOF) inertial measurement unit (IMU) in a single package, specifically developed as an eCompass device. Due to the IC housing a 3-axis accelerometer and a 3-axis magnetometer combined with its low cost, the LSM303C was perfect for us to create this small breakout board just for you! Each LSM303C Breakout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
