# Fritzing sketch Temperature and humidity sensor experiment (saved by Fritzing 0.9.3b)

parts:
  D1 = Rectifier Diode [part_number=1N4001 package="300 mil [THT]"]  # not connected
  S1 = Tilt Switch [package=THT]
  U1 = Mystery Part - 3 pins [chip_label=? package=THT]
  ANT1 = Antenna

nets:
  N1: S1.pin_49, ANT1.pin_3
  N2: S1.pin_50, ANT1.antenna_lead
  N3: S1.pin_51, ANT1.pin_1
  N4: S1.pin_62, S1.pin_63
  N5: S1.pin_106, U1.pin2
  N6: S1.pin_107, U1.pin1
  N7: S1.pin_108, U1.pin3
  N8: S1.pin_109, U1.pin_4

custom parts:
  Rectifier Diode: A standard rectifier diode
  Mystery Part - 3 pins: A dummy, proxy, ersatz, stand-in part for whatever you want. With 3 pins on a 100 mil inline pin header footprint.
  Antenna: Random Wire Antenna
