# Fritzing sketch LM35 temperature sensor experiment (saved by Fritzing 0.9.3b)
breadboards: 1

parts:
  D1 = Rectifier Diode [part_number=1N4001 package="300 mil [THT]"]  # not connected
  S1 = Tilt Switch [package=THT]
  T1 = LM35 Temperature Sensor [package="TO92 [THT]"]

nets:
  N1: S1.pin_64, T1.GND
  N2: S1.pin_65, T1.+Vs
  N3: S1.pin_66, T1.Vout

custom parts:
  Rectifier Diode: A standard rectifier diode
